# Fritzing sketch tripper-puck (saved by Fritzing 1.0.7)

parts:
  BK1 = E-bike (Talaria)
  BEC1 = 5 V BEC 3 A
  J1 = M8 4-pin (bike)
  U2 = SN65HVD230 CAN transceiver
  U3 = Gravity 10DOF (BNO055+BMP280)
  R1 = 2.2 k
  R2 = 2.2 k
  R3 = 10 k
  R4 = 10 k
  C1 = 100 nF
  C2 = 100 nF
  J2 = M12 8-pin (handlebar)
  DS1 = SSD1306 OLED 128x32
  U4 = u-blox NEO-8M (GYGPSV1)
  C3 = 100 uF
  SW1 = Push button
  SW2 = Push button
  U1 = XIAO ESP32-S3

nets:
  N1: BK1.PACK+, BEC1.VIN
  N2: BK1.PACK-, BEC1.GNDIN
  N3: BK1.CAN_H, J1.3_CAN_H
  N4: BK1.CAN_L, J1.4_CAN_L
  N5: BEC1.VOUT, J1.1_+5V
  N6: BEC1.GNDOUT, J1.2_GND
  N7: J1.1, U1.5V
  GND: J1.2, U2.GND, U3.GND, C1.2, C2.2, J2.2_GND, U1.GND
  N8: J1.3, U2.CANH
  N9: J1.4, U2.CANL
  3V3: U2.3V3, U3.VCC, R1.2, R2.2, R3.2, R4.2, J2.1_3V3, U1.3V3
  N10: U2.CTX, U1.D8
  N11: U2.CRX, U1.D9
  N12: U3.SDA, U1.D4
  N13: U3.SCL, U1.D5
  N14: R1.1, J2.3_SDA, U1.D3
  N15: R2.1, J2.4_SCK, U1.D10
  N16: R3.1, C1.1, J2.7_BTN1, U1.D1
  N17: R4.1, C2.1, J2.8_BTN2, U1.D2
  N18: J2.5_GPS_RX, U1.D6
  N19: J2.6_GPS_TX, U1.D7
  VCC: J2.1, DS1.VCC, U4.VCC, C3.+
  GND_2: J2.2, DS1.GND, U4.GND, C3.-, SW1.2, SW2.2
  N20: J2.3, DS1.SDA
  N21: J2.4, DS1.SCK
  N22: J2.5, U4.RX
  N23: J2.6, U4.TX
  N24: J2.7, SW1.1
  N25: J2.8, SW2.1

notes:
  HANDLEBAR
  REAR
  CONTROLLER + PACK

custom parts:
  E-bike (Talaria): E-bike (Talaria) — Tripper Puck DL1
  5 V BEC 3 A: 5 V BEC 3 A — Tripper Puck DL1
  M8 4-pin (bike): M8 4-pin (bike) — Tripper Puck DL1
  SN65HVD230 CAN transceiver: SN65HVD230 CAN transceiver — Tripper Puck DL1
  Gravity 10DOF (BNO055+BMP280): Gravity 10DOF (BNO055+BMP280) — Tripper Puck DL1
  2.2 k: 2.2 k — Tripper Puck DL1
  10 k: 10 k — Tripper Puck DL1
  100 nF: 100 nF — Tripper Puck DL1
  M12 8-pin (handlebar): M12 8-pin (handlebar) — Tripper Puck DL1
  SSD1306 OLED 128x32: SSD1306 OLED 128x32 — Tripper Puck DL1
  u-blox NEO-8M (GYGPSV1): u-blox NEO-8M (GYGPSV1) — Tripper Puck DL1
  100 uF: 100 uF — Tripper Puck DL1
  Push button: Push button — Tripper Puck DL1
  XIAO ESP32-S3: XIAO ESP32-S3 — Tripper Puck DL1
